// Digital circuit ALU_testbed.dig as structural Verilog
module ALU_testbed (
  input  [7:0] AHI,
  input  [7:0] BHI,
  input  [7:0] ALI,
  input  [7:0] BLI,
  input  standalone,
  input  clk,
  input  in_7,
  input  RLOE,
  input  SFW,
  input  SNH,
  input  RHOE,
  input  SNL
);

  wire _7402_2_pin1, _7402_2_pin4, _7402_2_pin10, _7402_2_pin13, _7408_1_pin4, _7408_1_pin5, _7408_1_pin6,
       _7408_1_pin8, _7408_1_pin9, _7408_1_pin10, _7408_1_pin11, _7408_2_pin3, _7408_2_pin10, _7414_1_pin2,
       _7414_1_pin8, _7414_1_pin9, _7414_1_pin11, _7414_2_pin4, _7414_2_pin6, _7414_2_pin9, _7414_2_pin12,
       _7486_1_pin2, _74132_1__1y, _74132_1__2y, _74132_1__3y, _74245_1_pin19, _74245_3_pin19, _74245_4_pin2,
       _74245_4_pin3, _74245_4_pin4, _74245_4_pin5, _74245_4_pin6, _74245_4_pin7, _74245_4_pin8,
       _74245_4_pin9, _74245_6_pin19, _74245_11_pin3, _74245_11_pin4, _74245_11_pin5, _74245_11_pin6,
       _74245_11_pin7, _74245_11_pin8, _74245_11_pin9, _74245_11_pin17, _74245_16_pin2, _74245_16_pin3,
       _74245_16_pin4, _74245_16_pin5, _74245_16_pin6, _74245_16_pin7, _74245_16_pin8, _74245_16_pin9,
       _74273_2_pin4, _74273_2_pin7, _74283_1_pin2, _74283_1_pin6, _74283_1_pin7, _74283_1_pin9,
       _74283_1_pin11, _74283_1_pin15, _74283_2_pin2, _74283_2_pin6, _74283_2_pin7, _74283_2_pin11,
       _74283_2_pin15, _74283_3_pin2, _74283_3_pin6, _74283_3_pin7, _74283_3_pin11, _74283_3_pin15,
       _74283_4_pin2, _74283_4_pin6, _74283_4_pin11, _74283_4_pin15, CFH, CFL, SFH, SFL, ZFH, ZFL;
  wire [7:0] _74245_1_pin3, _74245_1_pin18, _74245_2_pin9, _74245_5_pin2, _74245_5_pin11, _74245_8_pin2,
       _74245_9_pin2, _74245_9_pin11, _74245_10_pin2, _74245_13_pin2, _74245_13_pin11, _74245_15_pin2,
       _74273_1_pin2, _74273_3_pin12, IBHO, IBLO;
  wire [15:0] _74273_1_pin8;

  _74245 _74245_1 (
    .pin1(1'b0), .pin2(_74245_1_pin3[0]), .pin3(_74245_1_pin3[1]), .pin4(_74245_1_pin3[2]),
    .pin5(_74245_1_pin3[3]), .pin6(_74245_1_pin3[4]), .pin7(_74245_1_pin3[5]), .pin8(_74245_1_pin3[6]),
    .pin9(_74245_1_pin3[7]), .pin10(1'b0), .pin11(_74245_1_pin18[7]), .pin12(_74245_1_pin18[6]),
    .pin13(_74245_1_pin18[5]), .pin14(_74245_1_pin18[4]), .pin15(_74245_1_pin18[3]),
    .pin16(_74245_1_pin18[2]), .pin17(_74245_1_pin18[1]), .pin18(_74245_1_pin18[0]), .pin19(_74245_1_pin19),
    .pin20(1'b1));
  _74245 _74245_2 (
    .pin1(1'b0), .pin2(_74245_2_pin9[0]), .pin3(_74245_2_pin9[1]), .pin4(_74245_2_pin9[2]),
    .pin5(_74245_2_pin9[3]), .pin6(_74245_2_pin9[4]), .pin7(_74245_2_pin9[5]), .pin8(_74245_2_pin9[6]),
    .pin9(_74245_2_pin9[7]), .pin10(1'b0), .pin11(_74245_1_pin3[7]), .pin12(_74245_1_pin3[6]),
    .pin13(_74245_1_pin3[5]), .pin14(_74245_1_pin3[4]), .pin15(_74245_1_pin3[3]), .pin16(_74245_1_pin3[2]),
    .pin17(_74245_1_pin3[1]), .pin18(_74245_1_pin3[0]), .pin19(1'b0), .pin20(1'b1));
  LED led_1 (.in(_74245_2_pin9[7]));
  DipSwitch _3 (.out(_74245_1_pin18[5]));
  DipSwitch _2 (.out(_74245_1_pin18[6]));
  DipSwitch _1 (.out(_74245_1_pin18[7]));
  LED led_2 (.in(_74245_2_pin9[6]));
  LED led_3 (.in(_74245_2_pin9[5]));
  DipSwitch _7 (.out(_74245_1_pin18[1]));
  DipSwitch _6 (.out(_74245_1_pin18[2]));
  DipSwitch _5 (.out(_74245_1_pin18[3]));
  DipSwitch _4 (.out(_74245_1_pin18[4]));
  LED led_4 (.in(_74245_2_pin9[4]));
  LED led_5 (.in(_74245_2_pin9[3]));
  DipSwitch _8 (.out(_74245_1_pin18[0]));
  LED led_6 (.in(_74245_2_pin9[2]));
  LED led_7 (.in(_74245_2_pin9[1]));
  LED led_8 (.in(_74245_2_pin9[0]));
  _74245 _74245_3 (
    .pin1(1'b0), .pin2(_74245_1_pin3[0]), .pin3(_74245_1_pin3[1]), .pin4(_74245_1_pin3[2]),
    .pin5(_74245_1_pin3[3]), .pin6(_74245_1_pin3[4]), .pin7(_74245_1_pin3[5]), .pin8(_74245_1_pin3[6]),
    .pin9(_74245_1_pin3[7]), .pin10(1'b0), .pin11(AHI[7]), .pin12(AHI[6]), .pin13(AHI[5]), .pin14(AHI[4]),
    .pin15(AHI[3]), .pin16(AHI[2]), .pin17(AHI[1]), .pin18(AHI[0]), .pin19(_74245_3_pin19), .pin20(1'b1));
  _74273 _74273_1 (
    .pin1(in_7), .pin2(_74273_1_pin2[0]), .pin3(_74273_1_pin8[15]), .pin4(_74273_1_pin8[14]),
    .pin5(_74273_1_pin2[1]), .pin6(_74273_1_pin2[2]), .pin7(_74273_1_pin8[13]), .pin8(_74273_1_pin8[12]),
    .pin9(_74273_1_pin2[3]), .pin10(1'b0), .pin11(clk), .pin12(_74273_1_pin2[4]), .pin13(_74273_1_pin8[11]),
    .pin14(_74273_1_pin8[10]), .pin15(_74273_1_pin2[5]), .pin16(_74273_1_pin2[6]), .pin17(_74273_1_pin8[9]),
    .pin18(_74273_1_pin8[8]), .pin19(_74273_1_pin2[7]), .pin20(1'b1));
  _74245 _74245_4 (
    .pin1(1'b0), .pin2(_74245_4_pin2), .pin3(_74245_4_pin3), .pin4(_74245_4_pin4), .pin5(_74245_4_pin5),
    .pin6(_74245_4_pin6), .pin7(_74245_4_pin7), .pin8(_74245_4_pin8), .pin9(_74245_4_pin9), .pin10(1'b0),
    .pin11(_74273_1_pin2[7]), .pin12(_74273_1_pin2[6]), .pin13(_74273_1_pin2[5]), .pin14(_74273_1_pin2[4]),
    .pin15(_74273_1_pin2[3]), .pin16(_74273_1_pin2[2]), .pin17(_74273_1_pin2[1]), .pin18(_74273_1_pin2[0]),
    .pin19(1'b0), .pin20(1'b1));
  LED led_9 (.in(_74245_4_pin2));
  LED led_10 (.in(_74245_4_pin3));
  LED led_11 (.in(_74245_4_pin4));
  LED led_12 (.in(_74245_4_pin5));
  LED led_13 (.in(_74245_4_pin6));
  _74283 _74283_1 (
    .pin1(_74273_1_pin8[13]), .pin2(_74283_1_pin2), .pin3(_74245_1_pin3[5]), .pin4(_74273_1_pin8[12]),
    .pin5(_74245_1_pin3[4]), .pin6(_74283_1_pin6), .pin7(_74283_1_pin7), .pin8(1'b0), .pin9(_74283_1_pin9),
    .pin10(_74273_1_pin8[15]), .pin11(_74283_1_pin11), .pin12(_74245_1_pin3[7]), .pin13(_74273_1_pin8[14]),
    .pin14(_74245_1_pin3[6]), .pin15(_74283_1_pin15), .pin16(1'b1));
  LED led_14 (.in(_74245_4_pin7));
  LED led_15 (.in(_74245_4_pin8));
  LED led_16 (.in(_74245_4_pin9));
  _74245 _74245_5 (
    .pin1(1'b0), .pin2(_74245_5_pin2[0]), .pin3(_74245_5_pin2[1]), .pin4(_74245_5_pin2[2]),
    .pin5(_74245_5_pin2[3]), .pin6(_74245_5_pin2[4]), .pin7(_74245_5_pin2[5]), .pin8(_74245_5_pin2[6]),
    .pin9(_74245_5_pin2[7]), .pin10(1'b0), .pin11(_74245_5_pin11[7]), .pin12(_74245_5_pin11[6]),
    .pin13(_74245_5_pin11[5]), .pin14(_74245_5_pin11[4]), .pin15(_74245_5_pin11[3]),
    .pin16(_74245_5_pin11[2]), .pin17(_74245_5_pin11[1]), .pin18(_74245_5_pin11[0]), .pin19(_74245_1_pin19),
    .pin20(1'b1));
  DipSwitch _1_2 (.out(_74245_5_pin11[7]));
  DipSwitch _5_2 (.out(_74245_5_pin11[3]));
  DipSwitch _4_2 (.out(_74245_5_pin11[4]));
  DipSwitch _3_2 (.out(_74245_5_pin11[5]));
  DipSwitch _2_2 (.out(_74245_5_pin11[6]));
  DipSwitch _7_2 (.out(_74245_5_pin11[1]));
  DipSwitch _6_2 (.out(_74245_5_pin11[2]));
  DipSwitch _8_2 (.out(_74245_5_pin11[0]));
  _74245 _74245_6 (
    .pin1(1'b0), .pin2(IBHO[0]), .pin3(IBHO[1]), .pin4(IBHO[2]), .pin5(IBHO[3]), .pin6(IBHO[4]),
    .pin7(IBHO[5]), .pin8(IBHO[6]), .pin9(IBHO[7]), .pin10(1'b0), .pin11(_74273_1_pin2[7]),
    .pin12(_74273_1_pin2[6]), .pin13(_74273_1_pin2[5]), .pin14(_74273_1_pin2[4]), .pin15(_74273_1_pin2[3]),
    .pin16(_74273_1_pin2[2]), .pin17(_74273_1_pin2[1]), .pin18(_74273_1_pin2[0]), .pin19(_74245_6_pin19),
    .pin20(1'b1));
  _7486 _7486_1 (
    .pin1(_74245_5_pin2[4]), .pin2(_7486_1_pin2), .pin3(_74283_1_pin6), .pin4(_74245_5_pin2[5]),
    .pin5(_7486_1_pin2), .pin6(_74283_1_pin2), .pin7(1'b0), .pin8(_74283_1_pin15), .pin9(_74245_5_pin2[6]),
    .pin10(_7486_1_pin2), .pin11(_74283_1_pin11), .pin12(_74245_5_pin2[7]), .pin13(_7486_1_pin2), .pin14(1'b1));
  _74283 _74283_2 (
    .pin1(_74273_1_pin8[9]), .pin2(_74283_2_pin2), .pin3(_74245_1_pin3[1]), .pin4(_74273_1_pin8[8]),
    .pin5(_74245_1_pin3[0]), .pin6(_74283_2_pin6), .pin7(_74283_2_pin7), .pin8(1'b0), .pin9(_74283_1_pin7),
    .pin10(_74273_1_pin8[11]), .pin11(_74283_2_pin11), .pin12(_74245_1_pin3[3]), .pin13(_74273_1_pin8[10]),
    .pin14(_74245_1_pin3[2]), .pin15(_74283_2_pin15), .pin16(1'b1));
  _74245 _74245_7 (
    .pin1(1'b0), .pin2(_74245_5_pin2[0]), .pin3(_74245_5_pin2[1]), .pin4(_74245_5_pin2[2]),
    .pin5(_74245_5_pin2[3]), .pin6(_74245_5_pin2[4]), .pin7(_74245_5_pin2[5]), .pin8(_74245_5_pin2[6]),
    .pin9(_74245_5_pin2[7]), .pin10(1'b0), .pin11(BHI[7]), .pin12(BHI[6]), .pin13(BHI[5]), .pin14(BHI[4]),
    .pin15(BHI[3]), .pin16(BHI[2]), .pin17(BHI[1]), .pin18(BHI[0]), .pin19(_74245_3_pin19), .pin20(1'b1));
  _74245 _74245_8 (
    .pin1(1'b0), .pin2(_74245_8_pin2[0]), .pin3(_74245_8_pin2[1]), .pin4(_74245_8_pin2[2]),
    .pin5(_74245_8_pin2[3]), .pin6(_74245_8_pin2[4]), .pin7(_74245_8_pin2[5]), .pin8(_74245_8_pin2[6]),
    .pin9(_74245_8_pin2[7]), .pin10(1'b0), .pin11(_74245_5_pin2[7]), .pin12(_74245_5_pin2[6]),
    .pin13(_74245_5_pin2[5]), .pin14(_74245_5_pin2[4]), .pin15(_74245_5_pin2[3]), .pin16(_74245_5_pin2[2]),
    .pin17(_74245_5_pin2[1]), .pin18(_74245_5_pin2[0]), .pin19(1'b0), .pin20(1'b1));
  LED led_17 (.in(_74245_8_pin2[7]));
  LED led_18 (.in(_74245_8_pin2[6]));
  LED led_19 (.in(_74245_8_pin2[5]));
  LED led_20 (.in(_74245_8_pin2[4]));
  _7408 _7408_1 (
    .pin1(1'b0), .pin2(1'b0), .pin4(_7408_1_pin4), .pin5(_7408_1_pin5), .pin6(_7408_1_pin6), .pin7(1'b0),
    .pin8(_7408_1_pin8), .pin9(_7408_1_pin9), .pin10(_7408_1_pin10), .pin11(_7408_1_pin11),
    .pin12(_7408_1_pin8), .pin13(_7408_1_pin6), .pin14(1'b1));  // open: pin3
  LED led_21 (.in(_74245_8_pin2[3]));
  LED led_22 (.in(_74245_8_pin2[2]));
  LED led_23 (.in(_74245_8_pin2[1]));
  LED led_24 (.in(_74245_8_pin2[0]));
  _7486 _7486_2 (
    .pin1(_74245_5_pin2[0]), .pin2(_7486_1_pin2), .pin3(_74283_2_pin6), .pin4(_74245_5_pin2[1]),
    .pin5(_7486_1_pin2), .pin6(_74283_2_pin2), .pin7(1'b0), .pin8(_74283_2_pin15), .pin9(_74245_5_pin2[2]),
    .pin10(_7486_1_pin2), .pin11(_74283_2_pin11), .pin12(_74245_5_pin2[3]), .pin13(_7486_1_pin2), .pin14(1'b1));
  _7402 _7402_1 (
    .pin1(_7408_1_pin5), .pin2(_74273_1_pin8[15]), .pin3(_74273_1_pin8[14]), .pin4(_7408_1_pin4),
    .pin5(_74273_1_pin8[13]), .pin6(_74273_1_pin8[12]), .pin7(1'b0), .pin8(_74273_1_pin8[8]),
    .pin9(_74273_1_pin8[9]), .pin10(_7408_1_pin9), .pin11(_74273_1_pin8[10]), .pin12(_74273_1_pin8[11]),
    .pin13(_7408_1_pin10), .pin14(1'b1));
  _7414 _7414_1 (
    .pin1(standalone), .pin2(_7414_1_pin2), .pin3(_7414_1_pin2), .pin4(_74245_3_pin19),
    .pin5(_74245_3_pin19), .pin6(_74245_1_pin19), .pin7(1'b0), .pin8(_7414_1_pin8), .pin9(_7414_1_pin9),
    .pin10(_7414_1_pin9), .pin11(_7414_1_pin11), .pin12(_7414_1_pin11), .pin13(standalone), .pin14(1'b1));
  _74132 _74132_1 (
    ._1A(_74273_2_pin4), ._1B(SFW), ._1Y(_74132_1__1y), ._2A(_7414_2_pin12), ._2B(_7486_1_pin2),
    ._2Y(_74132_1__2y), ._3B(RLOE), ._3A(RLOE), ._3Y(_74132_1__3y), ._4A(_74132_1__2y), ._4B(_74132_1__1y),
    ._4Y(_74283_2_pin7), .VCC(1'b1), .GND(1'b0));
  _7414 _7414_2 (
    .pin1(RHOE), .pin2(_74245_6_pin19), .pin3(SNL), .pin4(_7414_2_pin4), .pin5(_7414_2_pin4),
    .pin6(_7414_2_pin6), .pin7(1'b0), .pin8(_7486_1_pin2), .pin9(_7414_2_pin9), .pin10(_7414_2_pin9),
    .pin11(SNH), .pin12(_7414_2_pin12), .pin13(SFW), .pin14(1'b1));
  _74273 _74273_2 (
    .pin1(in_7), .pin2(SFL), .pin3(_74273_1_pin8[7]), .pin4(_74273_2_pin4), .pin5(CFL), .pin6(ZFL),
    .pin7(_74273_2_pin7), .pin8(_74273_1_pin8[15]), .pin9(SFH), .pin10(1'b0), .pin11(clk), .pin12(CFH),
    .pin13(_74283_1_pin9), .pin14(_7408_1_pin11), .pin15(ZFH), .pin17(1'b0), .pin18(1'b0), .pin20(1'b1));  // open: pin16, pin19
  LED led_25 (.in(SFL));
  LED led_26 (.in(ZFL));
  LED led_27 (.in(CFL));
  LED led_28 (.in(CFH));
  LED led_29 (.in(SFH));
  _7402 _7402_2 (
    .pin1(_7402_2_pin1), .pin2(_74273_1_pin8[7]), .pin3(_74273_1_pin8[6]), .pin4(_7402_2_pin4),
    .pin5(_74273_1_pin8[5]), .pin6(_74273_1_pin8[4]), .pin7(1'b0), .pin8(_74273_1_pin8[0]),
    .pin9(_74273_1_pin8[1]), .pin10(_7402_2_pin10), .pin11(_74273_1_pin8[2]), .pin12(_74273_1_pin8[3]),
    .pin13(_7402_2_pin13), .pin14(1'b1));
  LED led_30 (.in(ZFH));
  _74245 _74245_9 (
    .pin1(1'b0), .pin2(_74245_9_pin2[0]), .pin3(_74245_9_pin2[1]), .pin4(_74245_9_pin2[2]),
    .pin5(_74245_9_pin2[3]), .pin6(_74245_9_pin2[4]), .pin7(_74245_9_pin2[5]), .pin8(_74245_9_pin2[6]),
    .pin9(_74245_9_pin2[7]), .pin10(1'b0), .pin11(_74245_9_pin11[7]), .pin12(_74245_9_pin11[6]),
    .pin13(_74245_9_pin11[5]), .pin14(_74245_9_pin11[4]), .pin15(_74245_9_pin11[3]),
    .pin16(_74245_9_pin11[2]), .pin17(_74245_9_pin11[1]), .pin18(_74245_9_pin11[0]), .pin19(_7414_1_pin8),
    .pin20(1'b1));
  _74245 _74245_10 (
    .pin1(1'b0), .pin2(_74245_10_pin2[0]), .pin3(_74245_10_pin2[1]), .pin4(_74245_10_pin2[2]),
    .pin5(_74245_10_pin2[3]), .pin6(_74245_10_pin2[4]), .pin7(_74245_10_pin2[5]), .pin8(_74245_10_pin2[6]),
    .pin9(_74245_10_pin2[7]), .pin10(1'b0), .pin11(_74245_9_pin2[7]), .pin12(_74245_9_pin2[6]),
    .pin13(_74245_9_pin2[5]), .pin14(_74245_9_pin2[4]), .pin15(_74245_9_pin2[3]), .pin16(_74245_9_pin2[2]),
    .pin17(_74245_9_pin2[1]), .pin18(_74245_9_pin2[0]), .pin19(1'b0), .pin20(1'b1));
  LED led_31 (.in(_74245_10_pin2[7]));
  DipSwitch _3_3 (.out(_74245_9_pin11[5]));
  DipSwitch _2_3 (.out(_74245_9_pin11[6]));
  DipSwitch _1_3 (.out(_74245_9_pin11[7]));
  LED led_32 (.in(_74245_10_pin2[6]));
  LED led_33 (.in(_74245_10_pin2[5]));
  DipSwitch _7_3 (.out(_74245_9_pin11[1]));
  DipSwitch _6_3 (.out(_74245_9_pin11[2]));
  DipSwitch _5_3 (.out(_74245_9_pin11[3]));
  DipSwitch _4_3 (.out(_74245_9_pin11[4]));
  LED led_34 (.in(_74245_10_pin2[4]));
  LED led_35 (.in(_74245_10_pin2[3]));
  _74245 _74245_11 (
    .pin1(1'b0), .pin3(_74245_11_pin3), .pin4(_74245_11_pin4), .pin5(_74245_11_pin5), .pin6(_74245_11_pin6),
    .pin7(_74245_11_pin7), .pin8(_74245_11_pin8), .pin9(_74245_11_pin9), .pin10(1'b0), .pin11(RHOE),
    .pin12(RLOE), .pin13(SFW), .pin14(SNH), .pin15(SNL), .pin16(clk), .pin17(_74245_11_pin17), .pin18(1'b0),
    .pin19(1'b0), .pin20(1'b1));  // open: pin2
  DipSwitch _8_3 (.out(_74245_9_pin11[0]));
  LED led_36 (.in(_74245_10_pin2[2]));
  LED led_37 (.in(_74245_10_pin2[1]));
  not not_1 (_74245_11_pin17, in_7);
  LED RST (.in(_74245_11_pin3));
  LED u_CLK (.in(_74245_11_pin4));
  LED led_38 (.in(_74245_10_pin2[0]));
  LED u_SNL (.in(_74245_11_pin5));
  LED u_SNH (.in(_74245_11_pin6));
  LED u_SFW (.in(_74245_11_pin7));
  LED u_RLOE (.in(_74245_11_pin8));
  _74245 _74245_12 (
    .pin1(1'b0), .pin2(_74245_9_pin2[0]), .pin3(_74245_9_pin2[1]), .pin4(_74245_9_pin2[2]),
    .pin5(_74245_9_pin2[3]), .pin6(_74245_9_pin2[4]), .pin7(_74245_9_pin2[5]), .pin8(_74245_9_pin2[6]),
    .pin9(_74245_9_pin2[7]), .pin10(1'b0), .pin11(ALI[7]), .pin12(ALI[6]), .pin13(ALI[5]), .pin14(ALI[4]),
    .pin15(ALI[3]), .pin16(ALI[2]), .pin17(ALI[1]), .pin18(ALI[0]), .pin19(_7414_1_pin9), .pin20(1'b1));
  LED u_RHOE (.in(_74245_11_pin9));
  _7408 _7408_2 (
    .pin1(_7402_2_pin4), .pin2(_7402_2_pin1), .pin3(_7408_2_pin3), .pin4(1'b0), .pin5(1'b0), .pin7(1'b0),
    .pin8(_74273_2_pin7), .pin9(_7408_2_pin3), .pin10(_7408_2_pin10), .pin11(_7408_2_pin10),
    .pin12(_7402_2_pin13), .pin13(_7402_2_pin10), .pin14(1'b1));  // open: pin6
  _74283 _74283_3 (
    .pin1(_74273_1_pin8[5]), .pin2(_74283_3_pin2), .pin3(_74245_9_pin2[5]), .pin4(_74273_1_pin8[4]),
    .pin5(_74245_9_pin2[4]), .pin6(_74283_3_pin6), .pin7(_74283_3_pin7), .pin8(1'b0), .pin9(_74273_2_pin4),
    .pin10(_74273_1_pin8[7]), .pin11(_74283_3_pin11), .pin12(_74245_9_pin2[7]), .pin13(_74273_1_pin8[6]),
    .pin14(_74245_9_pin2[6]), .pin15(_74283_3_pin15), .pin16(1'b1));
  _74245 _74245_13 (
    .pin1(1'b0), .pin2(_74245_13_pin2[0]), .pin3(_74245_13_pin2[1]), .pin4(_74245_13_pin2[2]),
    .pin5(_74245_13_pin2[3]), .pin6(_74245_13_pin2[4]), .pin7(_74245_13_pin2[5]), .pin8(_74245_13_pin2[6]),
    .pin9(_74245_13_pin2[7]), .pin10(1'b0), .pin11(_74245_13_pin11[7]), .pin12(_74245_13_pin11[6]),
    .pin13(_74245_13_pin11[5]), .pin14(_74245_13_pin11[4]), .pin15(_74245_13_pin11[3]),
    .pin16(_74245_13_pin11[2]), .pin17(_74245_13_pin11[1]), .pin18(_74245_13_pin11[0]), .pin19(_7414_1_pin8),
    .pin20(1'b1));
  DipSwitch _1_4 (.out(_74245_13_pin11[7]));
  DipSwitch _5_4 (.out(_74245_13_pin11[3]));
  DipSwitch _4_4 (.out(_74245_13_pin11[4]));
  DipSwitch _3_4 (.out(_74245_13_pin11[5]));
  DipSwitch _2_4 (.out(_74245_13_pin11[6]));
  DipSwitch _7_4 (.out(_74245_13_pin11[1]));
  DipSwitch _6_4 (.out(_74245_13_pin11[2]));
  DipSwitch _8_4 (.out(_74245_13_pin11[0]));
  _7486 _7486_3 (
    .pin1(_74245_13_pin2[4]), .pin2(_7414_2_pin6), .pin3(_74283_3_pin6), .pin4(_74245_13_pin2[5]),
    .pin5(_7414_2_pin6), .pin6(_74283_3_pin2), .pin7(1'b0), .pin8(_74283_3_pin15), .pin9(_74245_13_pin2[6]),
    .pin10(_7414_2_pin6), .pin11(_74283_3_pin11), .pin12(_74245_13_pin2[7]), .pin13(_7414_2_pin6),
    .pin14(1'b1));
  _74283 _74283_4 (
    .pin1(_74273_1_pin8[1]), .pin2(_74283_4_pin2), .pin3(_74245_9_pin2[1]), .pin4(_74273_1_pin8[0]),
    .pin5(_74245_9_pin2[0]), .pin6(_74283_4_pin6), .pin7(_7414_2_pin6), .pin8(1'b0), .pin9(_74283_3_pin7),
    .pin10(_74273_1_pin8[3]), .pin11(_74283_4_pin11), .pin12(_74245_9_pin2[3]), .pin13(_74273_1_pin8[2]),
    .pin14(_74245_9_pin2[2]), .pin15(_74283_4_pin15), .pin16(1'b1));
  _74245 _74245_14 (
    .pin1(1'b0), .pin2(_74245_13_pin2[0]), .pin3(_74245_13_pin2[1]), .pin4(_74245_13_pin2[2]),
    .pin5(_74245_13_pin2[3]), .pin6(_74245_13_pin2[4]), .pin7(_74245_13_pin2[5]), .pin8(_74245_13_pin2[6]),
    .pin9(_74245_13_pin2[7]), .pin10(1'b0), .pin11(BLI[7]), .pin12(BLI[6]), .pin13(BLI[5]), .pin14(BLI[4]),
    .pin15(BLI[3]), .pin16(BLI[2]), .pin17(BLI[1]), .pin18(BLI[0]), .pin19(_7414_1_pin9), .pin20(1'b1));
  _74245 _74245_15 (
    .pin1(1'b0), .pin2(_74245_15_pin2[0]), .pin3(_74245_15_pin2[1]), .pin4(_74245_15_pin2[2]),
    .pin5(_74245_15_pin2[3]), .pin6(_74245_15_pin2[4]), .pin7(_74245_15_pin2[5]), .pin8(_74245_15_pin2[6]),
    .pin9(_74245_15_pin2[7]), .pin10(1'b0), .pin11(_74245_13_pin2[7]), .pin12(_74245_13_pin2[6]),
    .pin13(_74245_13_pin2[5]), .pin14(_74245_13_pin2[4]), .pin15(_74245_13_pin2[3]),
    .pin16(_74245_13_pin2[2]), .pin17(_74245_13_pin2[1]), .pin18(_74245_13_pin2[0]), .pin19(1'b0),
    .pin20(1'b1));
  _74273 _74273_3 (
    .pin1(in_7), .pin2(_74273_3_pin12[0]), .pin3(_74273_1_pin8[7]), .pin4(_74273_1_pin8[6]),
    .pin5(_74273_3_pin12[1]), .pin6(_74273_3_pin12[2]), .pin7(_74273_1_pin8[5]), .pin8(_74273_1_pin8[4]),
    .pin9(_74273_3_pin12[3]), .pin10(1'b0), .pin11(clk), .pin12(_74273_3_pin12[4]), .pin13(_74273_1_pin8[3]),
    .pin14(_74273_1_pin8[2]), .pin15(_74273_3_pin12[5]), .pin16(_74273_3_pin12[6]), .pin17(_74273_1_pin8[1]),
    .pin18(_74273_1_pin8[0]), .pin19(_74273_3_pin12[7]), .pin20(1'b1));
  _74245 _74245_16 (
    .pin1(1'b0), .pin2(_74245_16_pin2), .pin3(_74245_16_pin3), .pin4(_74245_16_pin4), .pin5(_74245_16_pin5),
    .pin6(_74245_16_pin6), .pin7(_74245_16_pin7), .pin8(_74245_16_pin8), .pin9(_74245_16_pin9), .pin10(1'b0),
    .pin11(_74273_3_pin12[7]), .pin12(_74273_3_pin12[6]), .pin13(_74273_3_pin12[5]),
    .pin14(_74273_3_pin12[4]), .pin15(_74273_3_pin12[3]), .pin16(_74273_3_pin12[2]),
    .pin17(_74273_3_pin12[1]), .pin18(_74273_3_pin12[0]), .pin19(1'b0), .pin20(1'b1));
  LED led_39 (.in(_74245_16_pin2));
  LED led_40 (.in(_74245_15_pin2[7]));
  LED led_41 (.in(_74245_15_pin2[6]));
  LED led_42 (.in(_74245_16_pin3));
  LED led_43 (.in(_74245_16_pin4));
  LED led_44 (.in(_74245_15_pin2[5]));
  LED led_45 (.in(_74245_15_pin2[4]));
  LED led_46 (.in(_74245_16_pin5));
  LED led_47 (.in(_74245_16_pin6));
  LED led_48 (.in(_74245_15_pin2[3]));
  LED led_49 (.in(_74245_15_pin2[2]));
  LED led_50 (.in(_74245_16_pin7));
  LED led_51 (.in(_74245_16_pin8));
  LED led_52 (.in(_74245_15_pin2[1]));
  LED led_53 (.in(_74245_15_pin2[0]));
  _7486 _7486_4 (
    .pin1(_74245_13_pin2[0]), .pin2(_7414_2_pin6), .pin3(_74283_4_pin6), .pin4(_74245_13_pin2[1]),
    .pin5(_7414_2_pin6), .pin6(_74283_4_pin2), .pin7(1'b0), .pin8(_74283_4_pin15), .pin9(_74245_13_pin2[2]),
    .pin10(_7414_2_pin6), .pin11(_74283_4_pin11), .pin12(_74245_13_pin2[3]), .pin13(_7414_2_pin6),
    .pin14(1'b1));
  LED led_54 (.in(_74245_16_pin9));
  _74245 _74245_17 (
    .pin1(1'b0), .pin2(IBLO[0]), .pin3(IBLO[1]), .pin4(IBLO[2]), .pin5(IBLO[3]), .pin6(IBLO[4]),
    .pin7(IBLO[5]), .pin8(IBLO[6]), .pin9(IBLO[7]), .pin10(1'b0), .pin11(_74273_3_pin12[7]),
    .pin12(_74273_3_pin12[6]), .pin13(_74273_3_pin12[5]), .pin14(_74273_3_pin12[4]),
    .pin15(_74273_3_pin12[3]), .pin16(_74273_3_pin12[2]), .pin17(_74273_3_pin12[1]),
    .pin18(_74273_3_pin12[0]), .pin19(_74132_1__3y), .pin20(1'b1));

  // Other names for the same wires on the sheet: nRST = in_7

  // Notes on the sheet:
  //   standalone: default 1
  //   AH
  //   RH
  //   BH
  //   FR
  //   AL
  //   RL
  //   BL
endmodule
